// Logisim project Control_Unit.circ as structural Verilog: 1 circuit, main circuit Control_Unit
module Control_Unit (
  input  [5:0] in_1,
  input  [5:0] in_2,
  output isJAL,
  output MemRead,
  output IsShamt,
  output MemWrite,
  output MemtoReg,
  output Jump,
  output RegWrite,
  output Branch,
  output BneOrBeq,
  output [3:0] ALUop,
  output RegDst,
  output ALUSrc,
  output IsJR,
  output IsSyscall,
  output IsCOP0,
  output ZeroExtend,
  output ReadRs,
  output ReadRt
);

  wire funct_decoder_1_isjr, funct_decoder_1_isshamt, funct_decoder_1_issyscall, IsSpecial, not_1_out;
  wire [3:0] alu_decoder_1_p4, funct_decoder_1_alu0;

  Opcode_decoder opcode_decoder_1 (
    .op2(in_1[3]), .op3(in_1[2]), .op4(in_1[1]), .op5(in_1[0]), .op0(in_1[5]), .op1(in_1[4]), .Jump(Jump),
    .MemtoReg(MemtoReg), .MemWrite(MemWrite), .Branch(Branch), .RegDst(RegDst), .RegWrite(RegWrite),
    .BneBeq(BneOrBeq), .IsJAL(isJAL), .ZeroExtend(ZeroExtend), .ALUSrc(ALUSrc), .MemRead(MemRead));
  RegisterRead_Detector registerread_detector_1 (
    .op2(in_1[3]), .op3(in_1[2]), .op4(in_1[1]), .op5(in_1[0]), .Funct0(in_2[5]), .Funct1(in_2[4]),
    .op0(in_1[5]), .Funct2(in_2[3]), .Funct3(in_2[2]), .Funct4(in_2[1]), .Funct5(in_2[0]), .op1(in_1[4]),
    .ReadRs(ReadRs), .ReadRt(ReadRt));
  Funct_Decoder funct_decoder_1 (
    .Funct1(in_2[1]), .Funct2(in_2[2]), .Funct3(in_2[3]), .Funct4(in_2[4]), .Funct5(in_2[5]),
    .Funct0(in_2[0]), .ALU2(funct_decoder_1_alu0[2]), .ALU3(funct_decoder_1_alu0[3]),
    .IsJR(funct_decoder_1_isjr), .IsSyscall(funct_decoder_1_issyscall), .ALU0(funct_decoder_1_alu0[0]),
    .IsShamt(funct_decoder_1_isshamt), .ALU1(funct_decoder_1_alu0[1]));
  // ALU_Decoder alu_decoder_1: pin names not known; wires that end beside it: alu_decoder_1_p4[3], alu_decoder_1_p4[2], alu_decoder_1_p4[1], alu_decoder_1_p4[0]
  and and_1 (IsCOP0, ~in_1[0], in_1[1], ~in_1[2], ~in_1[3], ~in_1[4], ~in_1[5]);  // AND_Gate
  Multiplexer multiplexer_1 (.in0(1'b0), .in1(funct_decoder_1_issyscall), .out(IsSyscall), .sel(IsSpecial));
  Multiplexer multiplexer_2 (.in0(1'b0), .in1(funct_decoder_1_isjr), .out(IsJR), .sel(IsSpecial));
  Multiplexer multiplexer_3 (.in0(1'b0), .in1(funct_decoder_1_isshamt), .out(IsShamt), .sel(IsSpecial));
  not not_1 (not_1_out, IsSpecial);
  Multiplexer #(.width(4)) multiplexer_4 (
    .in0(funct_decoder_1_alu0), .in1(alu_decoder_1_p4), .out(ALUop), .sel(not_1_out));
  and and_2 (IsSpecial, ~in_1[0], ~in_1[1], ~in_1[2], ~in_1[3], ~in_1[4], ~in_1[5]);  // AND_Gate

  // Other names for the same wires on the sheet: Funct[5:0] = in_2; op[5:0] = in_1

  // Notes on the sheet:
  //   Input & Output
  //   OP Decoding Area
  //   ALU Decoding Area
  //   Exception Handler
endmodule
