// Logisim project Instruction_Statistics.circ as structural Verilog: 1 circuit, main circuit Instruction_Statistics
module Instruction_Statistics (
  input  op0,
  input  op1,
  input  op2,
  input  op3,
  input  op4,
  input  op5,
  output i,
  output r,
  output j
);

  wire and_1_out, and_2_out, and_3_out, and_4_out, and_5_out, and_6_out, and_7_out, and_8_out, and_9_out,
       and_10_out, and_12_out, and_13_out, not_1_out, not_2_out, not_3_out, not_4_out, not_5_out, not_6_out,
       not_7_out, not_8_out, not_9_out, not_10_out, not_11_out, not_12_out, not_13_out, not_14_out,
       not_15_out, not_16_out, not_17_out, not_18_out, not_19_out, not_20_out, not_21_out, not_22_out,
       not_23_out, not_24_out, not_25_out, not_26_out, not_27_out, not_28_out, not_29_out, not_30_out,
       not_31_out, not_32_out, not_33_out, not_34_out, not_35_out, not_36_out, not_37_out, not_38_out,
       not_39_out, not_40_out, not_41_out, not_42_out, not_43_out, not_44_out, not_45_out, not_46_out,
       not_47_out, not_48_out, not_49_out, not_50_out, not_51_out, not_52_out, not_53_out, not_54_out;

  not not_1 (not_1_out, op1);
  not not_2 (not_2_out, op2);
  not not_3 (not_3_out, op3);
  not not_4 (not_4_out, op1);
  not not_5 (not_5_out, op3);
  not not_6 (not_6_out, op0);
  not not_7 (not_7_out, op1);
  not not_8 (not_8_out, op2);
  not not_9 (not_9_out, op4);
  not not_10 (not_10_out, op0);
  not not_11 (not_11_out, op1);
  not not_12 (not_12_out, op2);
  not not_13 (not_13_out, op4);
  not not_14 (not_14_out, op5);
  not not_15 (not_15_out, op0);
  not not_16 (not_16_out, op1);
  not not_17 (not_17_out, op4);
  not not_18 (not_18_out, op5);
  not not_19 (not_19_out, op0);
  not not_20 (not_20_out, op1);
  not not_21 (not_21_out, op4);
  not not_22 (not_22_out, op0);
  not not_23 (not_23_out, op1);
  not not_24 (not_24_out, op3);
  not not_25 (not_25_out, op5);
  not not_26 (not_26_out, op0);
  not not_27 (not_27_out, op1);
  not not_28 (not_28_out, op3);
  not not_29 (not_29_out, op4);
  not not_30 (not_30_out, op5);
  not not_31 (not_31_out, op0);
  not not_32 (not_32_out, op1);
  not not_33 (not_33_out, op3);
  not not_34 (not_34_out, op4);
  not not_35 (not_35_out, op0);
  not not_36 (not_36_out, op1);
  not not_37 (not_37_out, op3);
  not not_38 (not_38_out, op4);
  not not_39 (not_39_out, op5);
  not not_40 (not_40_out, op0);
  not not_41 (not_41_out, op1);
  not not_42 (not_42_out, op2);
  not not_43 (not_43_out, op3);
  not not_44 (not_44_out, op4);
  not not_45 (not_45_out, op5);
  not not_46 (not_46_out, op0);
  not not_47 (not_47_out, op1);
  not not_48 (not_48_out, op2);
  not not_49 (not_49_out, op3);
  not not_50 (not_50_out, op5);
  not not_51 (not_51_out, op0);
  not not_52 (not_52_out, op1);
  not not_53 (not_53_out, op2);
  not not_54 (not_54_out, op3);
  and and_1 (and_1_out, op0, not_1_out, not_2_out, not_3_out, op4, op5);
  and and_2 (and_2_out, op0, not_4_out, op2, not_5_out, op4, op5);
  and and_3 (and_3_out, not_6_out, not_7_out, not_8_out, op3, not_9_out, op5);
  and and_4 (and_4_out, not_10_out, not_11_out, not_12_out, op3, not_13_out, not_14_out);
  and and_5 (and_5_out, not_15_out, not_16_out, op2, op3, not_17_out, not_18_out);
  and and_6 (and_6_out, not_19_out, not_20_out, op2, op3, not_21_out, op5);
  and and_7 (and_7_out, not_22_out, not_23_out, op2, not_24_out, op4, not_25_out);
  and and_8 (and_8_out, not_26_out, not_27_out, op2, not_28_out, not_29_out, not_30_out);
  and and_9 (and_9_out, not_31_out, not_32_out, op2, not_33_out, not_34_out, op5);
  and and_10 (and_10_out, not_35_out, not_36_out, op2, not_37_out, not_38_out, not_39_out);
  and and_11 (r, not_40_out, not_41_out, not_42_out, not_43_out, not_44_out, not_45_out);
  and and_12 (and_12_out, not_46_out, not_47_out, not_48_out, not_49_out, op4, not_50_out);
  and and_13 (and_13_out, not_51_out, not_52_out, not_53_out, not_54_out, op4, op5);
  or or_1 (i, and_1_out, and_2_out, and_3_out, and_4_out, and_5_out, and_6_out, and_7_out, and_8_out, and_9_out, and_10_out);
  or or_2 (j, and_12_out, and_13_out);
endmodule
