// Logisim project Opcode_decoder.circ as structural Verilog: 1 circuit, main circuit Opcode_decoder
module Opcode_decoder (
  input  op0,
  input  op1,
  input  op2,
  input  op3,
  input  op4,
  input  op5,
  output MemRead,
  output MemWrite,
  output ALUSrc,
  output Jump,
  output MemtoReg,
  output Branch,
  output RegDst,
  output RegWrite,
  output BneBeq,
  output IsJAL,
  output ZeroExtend
);

  wire and_3_out, and_4_out, and_5_out, and_6_out, and_7_out, and_8_out, and_9_out, and_10_out, and_11_out,
       and_12_out, and_14_out, and_15_out, and_17_out, and_18_out, and_19_out, and_20_out, and_21_out,
       and_22_out, and_23_out, and_24_out, and_25_out, and_26_out, and_29_out, and_30_out, not_1_out,
       not_2_out, not_3_out, not_4_out, not_5_out, not_6_out, not_7_out, not_8_out, not_9_out, not_10_out,
       not_11_out, not_12_out, not_13_out, not_14_out, not_15_out, not_16_out, not_17_out, not_18_out,
       not_19_out, not_20_out, not_21_out, not_22_out, not_23_out, not_24_out, not_25_out, not_26_out,
       not_27_out, not_28_out, not_29_out, not_30_out, not_31_out, not_32_out, not_33_out, not_34_out,
       not_35_out, not_36_out, not_37_out, not_38_out, not_39_out, not_40_out, not_41_out, not_42_out,
       not_43_out, not_44_out, not_45_out, not_46_out, not_47_out, not_48_out, not_49_out, not_50_out,
       not_51_out, not_52_out, not_53_out, not_54_out, not_55_out, not_56_out, not_57_out, not_58_out,
       not_59_out, not_60_out, not_61_out, not_62_out, not_63_out, not_64_out, not_65_out, not_66_out,
       not_67_out, not_68_out, not_69_out, not_70_out, not_71_out, not_72_out, not_73_out, not_74_out,
       not_75_out, not_76_out, not_77_out, not_78_out, not_79_out, not_80_out, not_81_out, not_82_out,
       not_83_out, not_84_out, not_85_out, not_86_out, not_87_out, not_88_out, not_89_out, not_90_out,
       not_91_out, not_92_out, not_93_out, not_94_out, not_95_out, not_96_out, not_97_out, not_98_out,
       not_99_out, not_100_out, not_101_out, not_102_out, not_103_out, not_104_out, not_105_out, not_106_out,
       not_107_out, not_108_out, not_109_out, not_110_out, not_111_out, not_112_out, not_113_out,
       not_114_out, not_115_out, not_116_out, not_117_out, not_118_out, not_119_out;

  not not_1 (not_1_out, op1);
  not not_2 (not_2_out, op2);
  not not_3 (not_3_out, op3);
  not not_4 (not_4_out, op1);
  not not_5 (not_5_out, op3);
  not not_6 (not_6_out, op0);
  not not_7 (not_7_out, op1);
  not not_8 (not_8_out, op3);
  not not_9 (not_9_out, op4);
  not not_10 (not_10_out, op5);
  not not_11 (not_11_out, op1);
  not not_12 (not_12_out, op2);
  not not_13 (not_13_out, op3);
  not not_14 (not_14_out, op1);
  not not_15 (not_15_out, op3);
  not not_16 (not_16_out, op0);
  not not_17 (not_17_out, op1);
  not not_18 (not_18_out, op4);
  not not_19 (not_19_out, op5);
  not not_20 (not_20_out, op0);
  not not_21 (not_21_out, op1);
  not not_22 (not_22_out, op4);
  not not_23 (not_23_out, op0);
  not not_24 (not_24_out, op1);
  not not_25 (not_25_out, op3);
  not not_26 (not_26_out, op5);
  not not_27 (not_27_out, op0);
  not not_28 (not_28_out, op1);
  not not_29 (not_29_out, op3);
  not not_30 (not_30_out, op4);
  not not_31 (not_31_out, op0);
  not not_32 (not_32_out, op1);
  not not_33 (not_33_out, op3);
  not not_34 (not_34_out, op4);
  not not_35 (not_35_out, op5);
  not not_36 (not_36_out, op0);
  not not_37 (not_37_out, op1);
  not not_38 (not_38_out, op2);
  not not_39 (not_39_out, op3);
  not not_40 (not_40_out, op5);
  not not_41 (not_41_out, op0);
  not not_42 (not_42_out, op1);
  not not_43 (not_43_out, op2);
  not not_44 (not_44_out, op3);
  not not_45 (not_45_out, op1);
  not not_46 (not_46_out, op2);
  not not_47 (not_47_out, op3);
  not not_48 (not_48_out, op0);
  not not_49 (not_49_out, op1);
  not not_50 (not_50_out, op2);
  not not_51 (not_51_out, op4);
  not not_52 (not_52_out, op0);
  not not_53 (not_53_out, op1);
  not not_54 (not_54_out, op2);
  not not_55 (not_55_out, op4);
  not not_56 (not_56_out, op5);
  not not_57 (not_57_out, op0);
  not not_58 (not_58_out, op1);
  not not_59 (not_59_out, op2);
  not not_60 (not_60_out, op3);
  not not_61 (not_61_out, op4);
  not not_62 (not_62_out, op5);
  not not_63 (not_63_out, op0);
  not not_64 (not_64_out, op1);
  not not_65 (not_65_out, op2);
  not not_66 (not_66_out, op3);
  not not_67 (not_67_out, op4);
  not not_68 (not_68_out, op5);
  not not_69 (not_69_out, op0);
  not not_70 (not_70_out, op1);
  not not_71 (not_71_out, op3);
  not not_72 (not_72_out, op4);
  not not_73 (not_73_out, op5);
  not not_74 (not_74_out, op1);
  not not_75 (not_75_out, op2);
  not not_76 (not_76_out, op3);
  not not_77 (not_77_out, op0);
  not not_78 (not_78_out, op1);
  not not_79 (not_79_out, op4);
  not not_80 (not_80_out, op5);
  not not_81 (not_81_out, op0);
  not not_82 (not_82_out, op1);
  not not_83 (not_83_out, op4);
  not not_84 (not_84_out, op0);
  not not_85 (not_85_out, op1);
  not not_86 (not_86_out, op3);
  not not_87 (not_87_out, op5);
  not not_88 (not_88_out, op0);
  not not_89 (not_89_out, op1);
  not not_90 (not_90_out, op3);
  not not_91 (not_91_out, op4);
  not not_92 (not_92_out, op0);
  not not_93 (not_93_out, op1);
  not not_94 (not_94_out, op3);
  not not_95 (not_95_out, op4);
  not not_96 (not_96_out, op5);
  not not_97 (not_97_out, op0);
  not not_98 (not_98_out, op1);
  not not_99 (not_99_out, op2);
  not not_100 (not_100_out, op3);
  not not_101 (not_101_out, op0);
  not not_102 (not_102_out, op2);
  not not_103 (not_103_out, op3);
  not not_104 (not_104_out, op4);
  not not_105 (not_105_out, op5);
  not not_106 (not_106_out, op0);
  not not_107 (not_107_out, op1);
  not not_108 (not_108_out, op2);
  not not_109 (not_109_out, op4);
  not not_110 (not_110_out, op0);
  not not_111 (not_111_out, op1);
  not not_112 (not_112_out, op2);
  not not_113 (not_113_out, op3);
  not not_114 (not_114_out, op0);
  not not_115 (not_115_out, op1);
  not not_116 (not_116_out, op4);
  not not_117 (not_117_out, op0);
  not not_118 (not_118_out, op1);
  not not_119 (not_119_out, op5);
  and and_1 (MemRead, op0, not_1_out, not_2_out, not_3_out, op4, op5);
  and and_2 (MemWrite, op0, not_4_out, op2, not_5_out, op4, op5);
  and and_3 (and_3_out, not_6_out, not_7_out, op2, not_8_out, not_9_out, not_10_out);
  and and_4 (and_4_out, op0, not_11_out, not_12_out, not_13_out, op4, op5);
  and and_5 (and_5_out, op0, not_14_out, op2, not_15_out, op4, op5);
  and and_6 (and_6_out, not_16_out, not_17_out, op2, op3, not_18_out, not_19_out);
  and and_7 (and_7_out, not_20_out, not_21_out, op2, op3, not_22_out, op5);
  and and_8 (and_8_out, not_23_out, not_24_out, op2, not_25_out, op4, not_26_out);
  and and_9 (and_9_out, not_27_out, not_28_out, op2, not_29_out, not_30_out, op5);
  and and_10 (and_10_out, not_31_out, not_32_out, op2, not_33_out, not_34_out, not_35_out);
  and and_11 (and_11_out, not_36_out, not_37_out, not_38_out, not_39_out, op4, not_40_out);
  and and_12 (and_12_out, not_41_out, not_42_out, not_43_out, not_44_out, op4, op5);
  and and_13 (MemtoReg, op0, not_45_out, not_46_out, not_47_out, op4, op5);
  and and_14 (and_14_out, not_48_out, not_49_out, not_50_out, op3, not_51_out, op5);
  and and_15 (and_15_out, not_52_out, not_53_out, not_54_out, op3, not_55_out, not_56_out);
  and and_16 (RegDst, not_57_out, not_58_out, not_59_out, not_60_out, not_61_out, not_62_out);
  and and_17 (and_17_out, not_63_out, not_64_out, not_65_out, not_66_out, not_67_out, not_68_out);
  and and_18 (and_18_out, not_69_out, not_70_out, op2, not_71_out, not_72_out, not_73_out);
  and and_19 (and_19_out, op0, not_74_out, not_75_out, not_76_out, op4, op5);
  and and_20 (and_20_out, not_77_out, not_78_out, op2, op3, not_79_out, not_80_out);
  and and_21 (and_21_out, not_81_out, not_82_out, op2, op3, not_83_out, op5);
  and and_22 (and_22_out, not_84_out, not_85_out, op2, not_86_out, op4, not_87_out);
  and and_23 (and_23_out, not_88_out, not_89_out, op2, not_90_out, not_91_out, op5);
  and and_24 (and_24_out, not_92_out, not_93_out, op2, not_94_out, not_95_out, not_96_out);
  and and_25 (and_25_out, not_97_out, not_98_out, not_99_out, not_100_out, op4, op5);
  and and_26 (and_26_out, not_101_out, op1, not_102_out, not_103_out, not_104_out, not_105_out);
  and and_27 (BneBeq, not_106_out, not_107_out, not_108_out, op3, not_109_out, op5);
  and and_28 (IsJAL, not_110_out, not_111_out, not_112_out, not_113_out, op4, op5);
  and and_29 (and_29_out, not_114_out, not_115_out, op2, op3, not_116_out);
  and and_30 (and_30_out, not_117_out, not_118_out, op2, op3, op4, not_119_out);
  or or_1 (ALUSrc, and_3_out, and_4_out, and_5_out, and_6_out, and_7_out, and_8_out, and_9_out, and_10_out);
  or or_2 (Jump, and_11_out, and_12_out);
  or or_3 (Branch, and_14_out, and_15_out);
  or or_4 (RegWrite, and_17_out, and_18_out, and_19_out, and_20_out, and_21_out, and_22_out, and_23_out, and_24_out, and_25_out, and_26_out);
  or or_5 (ZeroExtend, and_29_out, and_30_out);
endmodule
